# Fritzing sketch ESP8266CayenneHumidityMonitor (saved by Fritzing 0.9.3b)
circuit board: 5.10034cm x 2.32351cm
breadboards: 1

parts:
  R1 = Resistor [tolerance=±5% resistance=270k package=THT]
  R2 = Resistor [tolerance=±5% resistance=10k package=THT]
  LED1 = LED - 5mm [color="Red (633nm)" package="5 mm [THT]"]
  R3 = Resistor [tolerance=±5% resistance=330 package=THT]
  WeMos_D1_Mini1 = WeMos D1 Mini
  S2 = Round Pushbutton
  S1 = SWITCH-DPDT [package=eg2211]
  DHT1 = DHT22 Humidity and Temperature Sensor
  BATT1 = 4xAA Switchable Battery Pack w/Bare Wire
  C2 = Capacitor Polarized [package=cpol-radial-10uf-25v]
  C1 = Capacitor Polarized [package=cpol-radial-100uf-25v]

nets:
  N1: R1.Pin_0, WeMos_D1_Mini1.A0
  N2: R1.Pin_1, WeMos_D1_Mini1.5V, S1.6, C2.+, C1.+
  N3: R2.Pin_0, WeMos_D1_Mini1.D2, DHT1.DATA
  3V3: R2.Pin_1, WeMos_D1_Mini1.3V3, DHT1.VDD
  N4: LED1.cathode, WeMos_D1_Mini1.G, S2.leg0, S1.3, DHT1.GND, C2.-, C1.-
  N5: LED1.anode, R3.Pin_1
  N6: R3.Pin_0, WeMos_D1_Mini1.D7
  N7: WeMos_D1_Mini1.D0, WeMos_D1_Mini1.RST
  N8: WeMos_D1_Mini1.D1, S2.leg1
  N9: S1.2, BATT1.NEG
  N10: S1.5, BATT1.POS

custom parts:
  4xAA Switchable Battery Pack w/Bare Wire: 4xAA Switchable Battery Pack with Bare Wire connection
